// Logisim project projetodeCircuitosGTNExtreme_final2.circ as structural Verilog: 10 circuits, main circuit main
module \cronômetro  (
  input  PauseX,
  input  Alt_temp,
  input  Mode,
  input  Clear,
  input  US,
  input  DS,
  input  UM,
  input  DM,
  output [3:0] out_9,
  output [3:0] out_10,
  output termino,
  output [3:0] out_12,
  output [3:0] out_13,
  output [3:0] out_14,
  output [3:0] out_15,
  output [3:0] out_16,
  output [3:0] out_17
);

  wire and_1_out, and_2_out, and_3_out, and_4_out, and_5_out, clock_1_out,
       comparador_de_termino_1_id__termino, comparator_1_eq, comparator_2_eq, comparator_3_eq,
       comparator_4_eq, d_ff_17_q, multiplexer_1_out, not_1_out, not_2_out, not_3_out, not_4_out, not_5_out,
       not_6_out, not_7_out, not_8_out, not_9_out, not_10_out, not_11_out, not_12_out, not_13_out,
       not_14_out, not_15_out, not_16_out, not_17_out, not_18_out;
  wire [3:0] multiplexer_2_out, multiplexer_3_out, multiplexer_4_out, multiplexer_5_out, multiplexer_6_out,
       multiplexer_7_out, multiplexer_8_out, multiplexer_9_out, multiplexer_10_out, multiplexer_11_out,
       multiplexer_12_out, multiplexer_13_out, subtractor_1_out, subtractor_2_out, subtractor_3_out,
       subtractor_4_out;

  Clock clock_1 (.out(clock_1_out));
  D_Flip_Flop d_ff_1 (
    .clk(clock_1_out), .D(subtractor_2_out[3]), .Q(out_9[3]), .preset(multiplexer_13_out[3]),
    .en(multiplexer_1_out), .reset(not_1_out));  // open: Qn
  not not_1 (not_1_out, multiplexer_13_out[3]);
  D_Flip_Flop d_ff_2 (
    .clk(comparator_1_eq), .D(subtractor_3_out[3]), .Q(out_12[3]), .preset(multiplexer_10_out[3]),
    .en(not_18_out), .reset(not_2_out));  // open: Qn
  not not_2 (not_2_out, multiplexer_10_out[3]);
  D_Flip_Flop d_ff_3 (
    .clk(comparator_2_eq), .D(subtractor_4_out[3]), .Q(out_14[3]), .preset(multiplexer_11_out[3]),
    .en(not_18_out), .reset(not_3_out));  // open: Qn
  not not_3 (not_3_out, multiplexer_11_out[3]);
  D_Flip_Flop d_ff_4 (
    .clk(comparator_3_eq), .D(subtractor_1_out[3]), .Q(out_16[3]), .preset(multiplexer_12_out[3]),
    .en(not_18_out), .reset(not_4_out));  // open: Qn
  not not_4 (not_4_out, multiplexer_12_out[3]);
  D_Flip_Flop d_ff_5 (
    .clk(clock_1_out), .D(subtractor_2_out[2]), .Q(out_9[2]), .preset(multiplexer_13_out[2]),
    .en(multiplexer_1_out), .reset(not_5_out));  // open: Qn
  not not_5 (not_5_out, multiplexer_13_out[2]);
  D_Flip_Flop d_ff_6 (
    .clk(comparator_1_eq), .D(subtractor_3_out[2]), .Q(out_12[2]), .preset(multiplexer_10_out[2]),
    .en(not_18_out), .reset(not_6_out));  // open: Qn
  not not_6 (not_6_out, multiplexer_10_out[2]);
  D_Flip_Flop d_ff_7 (
    .clk(comparator_2_eq), .D(subtractor_4_out[2]), .Q(out_14[2]), .preset(multiplexer_11_out[2]),
    .en(not_18_out), .reset(not_7_out));  // open: Qn
  not not_7 (not_7_out, multiplexer_11_out[2]);
  D_Flip_Flop d_ff_8 (
    .clk(comparator_3_eq), .D(subtractor_1_out[2]), .Q(out_16[2]), .preset(multiplexer_12_out[2]),
    .en(not_18_out), .reset(not_8_out));  // open: Qn
  not not_8 (not_8_out, multiplexer_12_out[2]);
  D_Flip_Flop d_ff_9 (
    .clk(clock_1_out), .D(subtractor_2_out[1]), .Q(out_9[1]), .preset(multiplexer_13_out[1]),
    .en(multiplexer_1_out), .reset(not_9_out));  // open: Qn
  not not_9 (not_9_out, multiplexer_13_out[1]);
  D_Flip_Flop d_ff_10 (
    .clk(comparator_1_eq), .D(subtractor_3_out[1]), .Q(out_12[1]), .preset(multiplexer_10_out[1]),
    .en(not_18_out), .reset(not_10_out));  // open: Qn
  not not_10 (not_10_out, multiplexer_10_out[1]);
  D_Flip_Flop d_ff_11 (
    .clk(comparator_2_eq), .D(subtractor_4_out[1]), .Q(out_14[1]), .preset(multiplexer_11_out[1]),
    .en(not_18_out), .reset(not_11_out));  // open: Qn
  not not_11 (not_11_out, multiplexer_11_out[1]);
  D_Flip_Flop d_ff_12 (
    .clk(comparator_3_eq), .D(subtractor_1_out[1]), .Q(out_16[1]), .preset(multiplexer_12_out[1]),
    .en(not_18_out), .reset(not_12_out));  // open: Qn
  not not_12 (not_12_out, multiplexer_12_out[1]);
  D_Flip_Flop d_ff_13 (
    .clk(clock_1_out), .D(subtractor_2_out[0]), .Q(out_9[0]), .preset(multiplexer_13_out[0]),
    .en(multiplexer_1_out), .reset(not_13_out));  // open: Qn
  not not_13 (not_13_out, multiplexer_13_out[0]);
  D_Flip_Flop d_ff_14 (
    .clk(comparator_1_eq), .D(subtractor_3_out[0]), .Q(out_12[0]), .preset(multiplexer_10_out[0]),
    .en(not_18_out), .reset(not_14_out));  // open: Qn
  not not_14 (not_14_out, multiplexer_10_out[0]);
  D_Flip_Flop d_ff_15 (
    .clk(comparator_2_eq), .D(subtractor_4_out[0]), .Q(out_14[0]), .preset(multiplexer_11_out[0]),
    .en(not_18_out), .reset(not_15_out));  // open: Qn
  not not_15 (not_15_out, multiplexer_11_out[0]);
  D_Flip_Flop d_ff_16 (
    .clk(comparator_3_eq), .D(subtractor_1_out[0]), .Q(out_16[0]), .preset(multiplexer_12_out[0]),
    .en(not_18_out), .reset(not_16_out));  // open: Qn
  not not_16 (not_16_out, multiplexer_12_out[0]);
  Multiplexer multiplexer_1 (
    .in0(not_18_out), .in1(not_17_out), .out(multiplexer_1_out), .sel(comparador_de_termino_1_id__termino));  // open: en
  not not_17 (not_17_out, d_ff_17_q);
  D_Flip_Flop d_ff_17 (
    .clk(comparador_de_termino_1_id__termino), .D(comparador_de_termino_1_id__termino), .Q(d_ff_17_q));  // open: Qn, preset, en, reset
  Hex_Digit_Display hex_digit_display_1 (.value(out_12));  // open: dp
  Hex_Digit_Display hex_digit_display_2 (.value(out_14));  // open: dp
  Hex_Digit_Display hex_digit_display_3 (.value(out_16));  // open: dp
  Hex_Digit_Display hex_digit_display_4 (.value(out_9));  // open: dp
  Subtractor #(.width(4)) subtractor_1 (.a(out_16), .b(4'b0001), .out(subtractor_1_out));  // open: bin, bout
  Subtractor #(.width(4)) subtractor_2 (.a(out_9), .b(4'b0001), .out(subtractor_2_out));  // open: bin, bout
  Subtractor #(.width(4)) subtractor_3 (.a(out_12), .b(4'b0001), .out(subtractor_3_out));  // open: bin, bout
  Subtractor #(.width(4)) subtractor_4 (.a(out_14), .b(4'b0001), .out(subtractor_4_out));  // open: bin, bout
  Comparator #(.width(4)) comparator_1 (.a(out_9), .b(4'b1111), .eq(comparator_1_eq));  // open: gt, lt
  Comparator #(.width(4)) comparator_2 (.a(out_12), .b(4'b1111), .eq(comparator_2_eq));  // open: gt, lt
  Comparator #(.width(4)) comparator_3 (.a(out_14), .b(4'b1111), .eq(comparator_3_eq));  // open: gt, lt
  Comparator #(.width(4)) comparator_4 (.a(out_16), .b(4'b1111), .eq(comparator_4_eq));  // open: gt, lt
  not not_18 (not_18_out, PauseX);
  Multiplexer #(.width(4)) multiplexer_2 (.in1(4'b0000), .out(multiplexer_2_out), .sel(and_4_out));  // open: in0, en
  and and_1 (and_1_out, Mode, DS);
  Multiplexer #(.width(4)) multiplexer_3 (.in1(4'b0000), .out(multiplexer_3_out), .sel(and_4_out));  // open: in0, en
  and and_2 (and_2_out, Mode, UM);
  Multiplexer #(.width(4)) multiplexer_4 (.in1(4'b0000), .out(multiplexer_4_out), .sel(and_4_out));  // open: in0, en
  and and_3 (and_3_out, Mode, DM);
  and and_4 (and_4_out, Mode, Clear);
  Multiplexer #(.width(4)) multiplexer_5 (.in1(4'b0000), .out(multiplexer_5_out), .sel(and_4_out));  // open: in0, en
  and and_5 (and_5_out, Mode, US);
  Multiplexer #(.width(4)) multiplexer_6 (
    .in0(multiplexer_2_out), .in1(4'b0101), .out(multiplexer_6_out), .sel(comparator_2_eq));  // open: en
  simulador_borda_de_subida_2 simulador_borda_de_subida_2_1 (.in_1(and_1_out), .out_2(out_13));
  Multiplexer #(.width(4)) multiplexer_7 (
    .in0(multiplexer_3_out), .in1(4'b1001), .out(multiplexer_7_out), .sel(comparator_3_eq));  // open: en
  simulador_borda_de_subida simulador_borda_de_subida_1 (.in_1(and_2_out), .out_2(out_15));
  Multiplexer #(.width(4)) multiplexer_8 (
    .in0(multiplexer_4_out), .in1(4'b0101), .out(multiplexer_8_out), .sel(comparator_4_eq));  // open: en
  simulador_borda_de_subida_2 simulador_borda_de_subida_2_2 (.in_1(and_3_out), .out_2(out_17));
  Multiplexer #(.width(4)) multiplexer_9 (
    .in0(multiplexer_5_out), .in1(4'b1001), .out(multiplexer_9_out), .sel(comparator_1_eq));  // open: en
  simulador_borda_de_subida simulador_borda_de_subida_2 (.in_1(and_5_out), .out_2(out_10));
  Multiplexer #(.width(4)) multiplexer_10 (
    .in0(multiplexer_6_out), .in1(out_13), .out(multiplexer_10_out), .sel(Alt_temp));  // open: en
  Multiplexer #(.width(4)) multiplexer_11 (
    .in0(multiplexer_7_out), .in1(out_15), .out(multiplexer_11_out), .sel(Alt_temp));  // open: en
  Multiplexer #(.width(4)) multiplexer_12 (
    .in0(multiplexer_8_out), .in1(out_17), .out(multiplexer_12_out), .sel(Alt_temp));  // open: en
  Multiplexer #(.width(4)) multiplexer_13 (
    .in0(multiplexer_9_out), .in1(out_10), .out(multiplexer_13_out), .sel(Alt_temp));  // open: en
  comparador_de_termino comparador_de_termino_1 (
    .in_2(out_9), .in_3(out_12), .in_4(out_14), .in_5(out_16), .ver_clear(Clear),
    .id__termino(comparador_de_termino_1_id__termino));
  D_Flip_Flop d_ff_18 (
    .clk(clock_1_out), .D(comparador_de_termino_1_id__termino), .Q(termino));  // open: Qn, preset, en, reset
endmodule

module simulador_borda_de_subida (
  input  in_1,
  output [3:0] out_2
);

  wire comparator_1_eq;
  wire [3:0] subtractor_1_out;

  D_Flip_Flop d_ff_1 (
    .clk(in_1), .D(subtractor_1_out[3]), .Q(out_2[3]), .preset(comparator_1_eq));  // open: Qn, en, reset
  D_Flip_Flop d_ff_2 (
    .clk(in_1), .D(subtractor_1_out[2]), .Q(out_2[2]), .reset(comparator_1_eq));  // open: Qn, preset, en
  D_Flip_Flop d_ff_3 (
    .clk(in_1), .D(subtractor_1_out[1]), .Q(out_2[1]), .reset(comparator_1_eq));  // open: Qn, preset, en
  D_Flip_Flop d_ff_4 (
    .clk(in_1), .D(subtractor_1_out[0]), .Q(out_2[0]), .preset(comparator_1_eq));  // open: Qn, en, reset
  Hex_Digit_Display hex_digit_display_1 (.value(out_2));  // open: dp
  Subtractor #(.width(4)) subtractor_1 (.a(out_2), .b(4'b0001), .out(subtractor_1_out));  // open: bin, bout
  Comparator #(.width(4)) comparator_1 (.a(out_2), .b(4'b1111), .eq(comparator_1_eq));  // open: gt, lt
endmodule

module simulador_borda_de_subida_2 (
  input  in_1,
  output [3:0] out_2
);

  wire comparator_1_eq;
  wire [3:0] subtractor_1_out;

  D_Flip_Flop d_ff_1 (
    .clk(in_1), .D(subtractor_1_out[3]), .Q(out_2[3]), .reset(comparator_1_eq));  // open: Qn, preset, en
  D_Flip_Flop d_ff_2 (
    .clk(in_1), .D(subtractor_1_out[2]), .Q(out_2[2]), .preset(comparator_1_eq));  // open: Qn, en, reset
  D_Flip_Flop d_ff_3 (
    .clk(in_1), .D(subtractor_1_out[1]), .Q(out_2[1]), .reset(comparator_1_eq));  // open: Qn, preset, en
  D_Flip_Flop d_ff_4 (
    .clk(in_1), .D(subtractor_1_out[0]), .Q(out_2[0]), .preset(comparator_1_eq));  // open: Qn, en, reset
  Hex_Digit_Display hex_digit_display_1 (.value(out_2));  // open: dp
  Subtractor #(.width(4)) subtractor_1 (.a(out_2), .b(4'b0001), .out(subtractor_1_out));  // open: bin, bout
  Comparator #(.width(4)) comparator_1 (.a(out_2), .b(4'b1111), .eq(comparator_1_eq));  // open: gt, lt
endmodule

module numero_escolhido (
  input  Clock,
  input  \próximo ,
  input  [3:0] num__escolh__A,
  input  [3:0] num__escolh__B,
  input  id__jogador,
  output [3:0] \saída 
);

  wire [3:0] multiplexer_1_out;

  Multiplexer #(.width(4)) multiplexer_1 (
    .in0(num__escolh__A), .in1(num__escolh__B), .out(multiplexer_1_out), .sel(id__jogador));  // open: en
  D_Flip_Flop d_ff_1 (
    .clk(Clock), .D(multiplexer_1_out[3]), .Q(\saída [3]), .en(\próximo ));  // open: Qn, preset, reset
  D_Flip_Flop d_ff_2 (
    .clk(Clock), .D(multiplexer_1_out[2]), .Q(\saída [2]), .en(\próximo ));  // open: Qn, preset, reset
  D_Flip_Flop d_ff_3 (
    .clk(Clock), .D(multiplexer_1_out[1]), .Q(\saída [1]), .en(\próximo ));  // open: Qn, preset, reset
  D_Flip_Flop d_ff_4 (
    .clk(Clock), .D(multiplexer_1_out[0]), .Q(\saída [0]), .en(\próximo ));  // open: Qn, preset, reset
endmodule

module ativador_sinal__Sx_Sy (
  input  [3:0] Entrada_original,
  input  s__J_A,
  input  S_J_B,
  output S,
  output [3:0] s__compl
);

  wire and_1_out, and_2_out;

  Negator #(.width(4)) negator_1 (.in(Entrada_original), .out(s__compl));
  or or_1 (S, and_1_out, and_2_out);
  and and_1 (and_1_out, s__compl[3], s__J_A);
  and and_2 (and_2_out, s__compl[3], S_J_B);
endmodule

module \máquina_estados__transição_de_jogadores  (
  input  clock,
  output Y,
  output X
);

  wire not_1_out, xor_1_out;

  xor xor_1 (xor_1_out, X, Y);
  not not_1 (not_1_out, Y);
  D_Flip_Flop d_ff_1 (.clk(clock), .D(xor_1_out), .Q(X));  // open: Qn, preset, en, reset
  D_Flip_Flop d_ff_2 (.clk(clock), .D(not_1_out), .Q(Y));  // open: Qn, preset, en, reset

  // Notes on the sheet:
  //   00 = jogador A, coordenada X (A,X)
  //   01 = jogador A, coordenada Y (A,Y)
  //   utilizar essa verificação de sinais para alternar as rodadas dos jogadores e verificar se o valor recebido correspondete ao jogador correto
  //   CODIFICAÇÃO DAS SAÍDAS
  //   (X,Y)
  //   10 = jogador B, coordenada X (B,X)
  //   11 = jogador B, coordenada Y (B,Y)
endmodule

module main (
  input  novo_P_oculto,
  input  Alt_temp,
  input  Alt_temp_2,
  input  Mode,
  input  Mode_2,
  input  PauseX,
  input  PauseX_2,
  input  clear,
  input  clear_2,
  input  \Próximo ,
  input  A3,
  input  A2,
  input  A1,
  input  A0,
  input  A3_2,
  input  A2_2,
  input  A1_2,
  input  A0_2,
  output Menor,
  output igual,
  output Maior,
  output Acertou
);

  wire and_1_out, and_2_out, and_3_out, and_4_out, and_5_out, ativador_sinal_sx_sy_1_s,
       ativador_sinal_sx_sy_2_s, Chutar_out, core_1_empate, core_1_fim_do_jogo, core_1_pontua_a,
       core_1_pontua_b, \core_1_vitória_a , \core_1_vitória_b , \cronômetro_1_termino ,
       \cronômetro_2_termino , d_ff_1_q, d_ff_2_q, d_ff_3_q, d_ff_4_q, DM_2_out, DM_out, DS_2_out, DS_out,
       \máquina_estados_transição_de_jogadores_1_x , \máquina_estados_transição_de_jogadores_1_y , not_1_out,
       not_2_out, not_3_out, not_4_out, not_5_out, or_1_out, or_2_out, UM_2_out, UM_out, US_2_out, US_out;
  wire [3:0] ativador_sinal_sx_sy_1_s__compl, ativador_sinal_sx_sy_2_s__compl, core_1_p__oculto, core_1_soma,
       counter_1_q, counter_2_q, \cronômetro_1_out_9 , \cronômetro_1_out_12 , \cronômetro_1_out_14 ,
       \cronômetro_1_out_16 , \cronômetro_2_out_9 , \cronômetro_2_out_12 , \cronômetro_2_out_14 ,
       \cronômetro_2_out_16 , multiplexer_1_out, multiplexer_2_out, multiplexer_3_out, multiplexer_4_out,
       multiplexer_5_out, multiplexer_6_out, negator_1_out, negator_2_out, \numero_escolhido_1_saída ,
       \numero_escolhido_2_saída ;

  Button US (.out(US_out));
  Button DS (.out(DS_out));
  Button UM (.out(UM_out));
  Button DM (.out(DM_out));
  Multiplexer #(.width(4)) multiplexer_1 (
    .in1({A3, A2, A1, A0}), .out(multiplexer_1_out), .sel(not_1_out));  // open: in0, en
  not not_1 (not_1_out, \cronômetro_1_termino );
  Hex_Digit_Display hex_digit_display_1 (.value(core_1_soma));  // open: dp
  or or_1 (or_1_out, PauseX, \máquina_estados_transição_de_jogadores_1_x );
  \cronômetro  \cronômetro_1  (
    .US(US_out), .DS(DS_out), .UM(UM_out), .DM(DM_out), .PauseX(or_1_out), .Alt_temp(Alt_temp_2),
    .Mode(Mode_2), .out_9(\cronômetro_1_out_9 ), .Clear(clear_2), .out_12(\cronômetro_1_out_12 ),
    .out_14(\cronômetro_1_out_14 ), .out_16(\cronômetro_1_out_16 ), .termino(\cronômetro_1_termino ));  // open: out_10, out_13, out_15, out_17
  LED SA (.in(A3));
  Negator #(.width(4)) negator_1 (.in(multiplexer_1_out), .out(negator_1_out));
  \máquina_estados__transição_de_jogadores  \máquina_estados_transição_de_jogadores_1  (
    .clock(Chutar_out), .Y(\máquina_estados_transição_de_jogadores_1_y ),
    .X(\máquina_estados_transição_de_jogadores_1_x ));
  not not_2 (not_2_out, \máquina_estados_transição_de_jogadores_1_x );
  Hex_Digit_Display hex_digit_display_2 (.value(\cronômetro_1_out_16 ));  // open: dp
  Hex_Digit_Display hex_digit_display_3 (.value(multiplexer_2_out));  // open: dp
  Multiplexer #(.width(4)) multiplexer_2 (
    .in0(multiplexer_1_out), .in1(negator_1_out), .out(multiplexer_2_out), .sel(A3));  // open: en
  LED A_jogando (.in(not_2_out));
  Hex_Digit_Display hex_digit_display_4 (.value(counter_1_q));  // open: dp
  Counter #(.width(4), .max('hf)) counter_1 (
    .count(core_1_pontua_a), .Q(counter_1_q), .clk(core_1_pontua_a));  // open: load, D, carry, clr
  Hex_Digit_Display hex_digit_display_5 (.value(\cronômetro_1_out_12 ));  // open: dp
  Hex_Digit_Display hex_digit_display_6 (.value(\cronômetro_1_out_14 ));  // open: dp
  Hex_Digit_Display hex_digit_display_7 (.value(multiplexer_3_out));  // open: dp
  Hex_Digit_Display hex_digit_display_8 (.value(\cronômetro_1_out_9 ));  // open: dp
  ativador_sinal__Sx_Sy ativador_sinal_sx_sy_1 (
    .Entrada_original(\numero_escolhido_1_saída ), .S(ativador_sinal_sx_sy_1_s), .s__J_A(d_ff_1_q),
    .S_J_B(d_ff_2_q), .s__compl(ativador_sinal_sx_sy_1_s__compl));
  numero_escolhido numero_escolhido_1 (
    .num__escolh__A(multiplexer_2_out), .num__escolh__B(multiplexer_5_out),
    .id__jogador(\máquina_estados_transição_de_jogadores_1_x ), .\saída (\numero_escolhido_1_saída ),
    .Clock(and_3_out), .\próximo (and_3_out));
  D_Flip_Flop d_ff_1 (.clk(and_3_out), .D(and_1_out), .Q(d_ff_1_q));  // open: Qn, preset, en, reset
  and and_1 (and_1_out, ~\máquina_estados_transição_de_jogadores_1_x , A3);  // AND_Gate
  D_Flip_Flop d_ff_2 (.clk(and_3_out), .D(and_2_out), .Q(d_ff_2_q));  // open: Qn, preset, en, reset
  and and_2 (and_2_out, \máquina_estados_transição_de_jogadores_1_x , A3_2);
  not not_3 (not_3_out, \Próximo );
  LED A_venceu (.in(\core_1_vitória_a ));
  Multiplexer #(.width(4)) multiplexer_3 (
    .in0(\numero_escolhido_1_saída ), .in1(ativador_sinal_sx_sy_1_s__compl), .out(multiplexer_3_out),
    .sel(ativador_sinal_sx_sy_1_s));  // open: en
  LED SX (.in(ativador_sinal_sx_sy_1_s));
  Hex_Digit_Display hex_digit_display_9 (.value(\numero_escolhido_1_saída ));  // open: dp
  LED Chutando_X (.in(not_3_out));
  LED Fim_do_jogo (.in(core_1_fim_do_jogo));
  LED Empate (.in(core_1_empate));
  core core_1 (
    .novo_P_oculto(novo_P_oculto), .chutar(Chutar_out), .X(\máquina_estados_transição_de_jogadores_1_x ),
    .Y(\máquina_estados_transição_de_jogadores_1_y ), .P__Oculto(core_1_p__oculto), .Maior(Maior),
    .chute_X(multiplexer_3_out), .Igual(igual), .Acertou(Acertou), .Menor(Menor),
    .chute_Y(multiplexer_4_out), .soma(core_1_soma), .pontua_A(core_1_pontua_a), .pontua_B(core_1_pontua_b),
    .pont_atual_A(counter_1_q), .id__termino_A(\cronômetro_1_termino ), .\Vitória_A (\core_1_vitória_a ),
    .Fim_do_jogo(core_1_fim_do_jogo), .id__termino_B(\cronômetro_2_termino ),
    .\Vitória_B (\core_1_vitória_b ), .pont_atual_B(counter_2_q), .Empate(core_1_empate), .proximp(\Próximo ));
  Button Chutar (.out(Chutar_out));
  and and_3 (and_3_out, Chutar_out, ~\Próximo );  // AND_Gate
  LED B_venceu (.in(\core_1_vitória_b ));
  LED SY (.in(ativador_sinal_sx_sy_2_s));
  Hex_Digit_Display hex_digit_display_10 (.value(\numero_escolhido_2_saída ));  // open: dp
  numero_escolhido numero_escolhido_2 (
    .num__escolh__A(multiplexer_2_out), .num__escolh__B(multiplexer_5_out),
    .id__jogador(\máquina_estados_transição_de_jogadores_1_x ), .\saída (\numero_escolhido_2_saída ),
    .Clock(Chutar_out), .\próximo (\Próximo ));
  D_Flip_Flop d_ff_3 (.clk(Chutar_out), .D(and_4_out), .Q(d_ff_3_q));  // open: Qn, preset, en, reset
  and and_4 (and_4_out, ~\máquina_estados_transição_de_jogadores_1_x , A3);  // AND_Gate
  D_Flip_Flop d_ff_4 (.clk(Chutar_out), .D(and_5_out), .Q(d_ff_4_q));  // open: Qn, preset, en, reset
  and and_5 (and_5_out, \máquina_estados_transição_de_jogadores_1_x , A3_2);
  Hex_Digit_Display hex_digit_display_11 (.value(core_1_p__oculto));  // open: dp
  Multiplexer #(.width(4)) multiplexer_4 (
    .in0(\numero_escolhido_2_saída ), .in1(ativador_sinal_sx_sy_2_s__compl), .out(multiplexer_4_out),
    .sel(ativador_sinal_sx_sy_2_s));  // open: en
  LED Chutando_Y (.in(\Próximo ));
  Hex_Digit_Display hex_digit_display_12 (.value(multiplexer_4_out));  // open: dp
  Button US_2 (.out(US_2_out));
  Button DS_2 (.out(DS_2_out));
  Button UM_2 (.out(UM_2_out));
  Button DM_2 (.out(DM_2_out));
  ativador_sinal__Sx_Sy ativador_sinal_sx_sy_2 (
    .Entrada_original(\numero_escolhido_2_saída ), .S(ativador_sinal_sx_sy_2_s), .s__J_A(d_ff_3_q),
    .S_J_B(d_ff_4_q), .s__compl(ativador_sinal_sx_sy_2_s__compl));
  or or_2 (or_2_out, PauseX_2, not_5_out);
  \cronômetro  \cronômetro_2  (
    .US(US_2_out), .DS(DS_2_out), .UM(UM_2_out), .DM(DM_2_out), .PauseX(or_2_out), .Alt_temp(Alt_temp),
    .Mode(Mode), .out_9(\cronômetro_2_out_9 ), .Clear(clear), .out_12(\cronômetro_2_out_12 ),
    .out_14(\cronômetro_2_out_14 ), .out_16(\cronômetro_2_out_16 ), .termino(\cronômetro_2_termino ));  // open: out_10, out_13, out_15, out_17
  LED B_jogando (.in(\máquina_estados_transição_de_jogadores_1_x ));
  Hex_Digit_Display hex_digit_display_13 (.value(\cronômetro_2_out_16 ));  // open: dp
  LED SB (.in(A3_2));
  Hex_Digit_Display hex_digit_display_14 (.value(multiplexer_5_out));  // open: dp
  Multiplexer #(.width(4)) multiplexer_5 (
    .in0(multiplexer_6_out), .in1(negator_2_out), .out(multiplexer_5_out), .sel(A3_2));  // open: en
  Counter #(.width(4), .max('hf)) counter_2 (
    .count(core_1_pontua_b), .Q(counter_2_q), .clk(core_1_pontua_b));  // open: load, D, carry, clr
  Hex_Digit_Display hex_digit_display_15 (.value(\cronômetro_2_out_14 ));  // open: dp
  Hex_Digit_Display hex_digit_display_16 (.value(\cronômetro_2_out_12 ));  // open: dp
  Multiplexer #(.width(4)) multiplexer_6 (
    .in1({A3_2, A2_2, A1_2, A0_2}), .out(multiplexer_6_out), .sel(not_4_out));  // open: in0, en
  not not_4 (not_4_out, \cronômetro_2_termino );
  Negator #(.width(4)) negator_2 (.in(multiplexer_6_out), .out(negator_2_out));
  Hex_Digit_Display hex_digit_display_17 (.value(counter_2_q));  // open: dp
  Hex_Digit_Display hex_digit_display_18 (.value(\cronômetro_2_out_9 ));  // open: dp
  not not_5 (not_5_out, \máquina_estados_transição_de_jogadores_1_x );

  // Notes on the sheet:
  //   10
  //   soma
  //   CRONÔMETRO A
  //   clicar em chutar e ir para 1, 
  //   número escolhido
  //   placar A
  //   chute X
  //   ponto oculto
  //   chute Y
  //   número escolhido
  //   CRONÔMETRO B
  //   placar B
endmodule

module core (
  input  novo_P_oculto,
  input  chutar,
  input  X,
  input  Y,
  input  [3:0] chute_X,
  input  [3:0] chute_Y,
  input  proximp,
  input  [3:0] pont_atual_A,
  input  id__termino_A,
  input  id__termino_B,
  input  [3:0] pont_atual_B,
  output [3:0] P__Oculto,
  output Maior,
  output Igual,
  output Acertou,
  output Menor,
  output [3:0] soma,
  output pontua_A,
  output pontua_B,
  output \Vitória_A ,
  output Fim_do_jogo,
  output \Vitória_B ,
  output Empate
);

  wire and_1_out, and_4_out, and_5_out, comparator_1_eq, comparator_2_eq, comparator_4_eq, comparator_4_gt,
       comparator_4_lt, not_1_out, or_4_out, xor_1_out;
  wire [3:0] multiplexer_1_out, \numero_core_2_1_saída , \numero_core_2_2_saída ;
  wire [7:0] random_1_out;

  numero_core_2 numero_core_2_1 (
    .num__escolh__B(chute_X), .Clock(chutar), .\saída (\numero_core_2_1_saída ));  // open: zerar_soma, próximo
  not not_1 (not_1_out, chutar);
  numero_core_2 numero_core_2_2 (
    .num__escolh__B(multiplexer_1_out), .Clock(not_1_out), .\saída (\numero_core_2_2_saída ));  // open: zerar_soma, próximo
  Multiplexer #(.width(4)) multiplexer_1 (.in1(chute_Y), .out(multiplexer_1_out), .sel(proximp));  // open: in0, en
  and and_1 (and_1_out, id__termino_A, id__termino_B);
  Random random_1 (.clk(or_4_out), .out(random_1_out));  // open: next, clr
  Comparator #(.width(4)) comparator_1 (.a(pont_atual_A), .b(4'b1111), .eq(comparator_1_eq));  // open: gt, lt
  Comparator #(.width(4)) comparator_2 (.a(pont_atual_B), .b(4'b1111), .eq(comparator_2_eq));  // open: gt, lt
  Adder #(.width(4)) adder_1 (.a(\numero_core_2_1_saída ), .b(\numero_core_2_2_saída ), .out(soma));  // open: cin, cout
  Comparator #(.width(4)) comparator_3 (.a(soma), .b(P__Oculto), .gt(Maior), .eq(Igual), .lt(Menor));
  or or_1 (Fim_do_jogo, comparator_1_eq, and_1_out, comparator_2_eq);
  Hex_Digit_Display hex_digit_display_1 (.value(P__Oculto));  // open: dp
  Adder #(.width(4)) adder_2 (.a(random_1_out[3:0]), .b(random_1_out[7:4]), .out(P__Oculto));  // open: cin, cout
  Comparator #(.width(4)) comparator_4 (
    .a(pont_atual_A), .b(pont_atual_B), .gt(comparator_4_gt), .eq(comparator_4_eq), .lt(comparator_4_lt));
  and and_2 (pontua_A, Igual, X);
  and and_3 (pontua_B, Igual, ~X);  // AND_Gate
  or or_2 (\Vitória_A , comparator_1_eq, and_4_out);
  and and_4 (and_4_out, comparator_4_gt, and_1_out);
  and and_5 (and_5_out, and_1_out, comparator_4_lt);
  or or_3 (\Vitória_B , and_5_out, comparator_2_eq);
  and and_6 (Empate, comparator_4_eq, and_1_out);
  xor xor_1 (xor_1_out, chutar, or_4_out);
  or or_4 (or_4_out, pontua_B, pontua_A);
  D_Flip_Flop d_ff_1 (.clk(xor_1_out), .D(or_4_out), .Q(Acertou));  // open: Qn, preset, en, reset

  // Notes on the sheet:
  //   verificar condições de término do jogo
  //   fazer o mesmo para o X só que se 10
  //   00 e 01 jogador A
  //   10 e 11 jogador B
  //   fazer outro comparador com borda de subida para
  //   estados jogadores
  //   colocar flip flop para captar entrada de x
  //   um novo ponto oculto é gerado quando um ciclo de rodadas termina
  //   chute X e chute Y só irão receber uma num se o sinal do mux estiver ativado
  //   00 chute de X do jogador A
  //   01 chute de Y do jogador A
  //   10 chute X do jogador B
  //   11 chute Y do jogador B
  //   ou seja, quando ambos jogarem, a máquina de estados retornar ao jogador A
  //   usar apenas um gerador de 8 bits, cujos bits sao divididos em dois conjuntos que são entradas do somador
  //   um para acender os led maior, menor e igual, e outro para acender especificamente acertou e gerar os novos pontos ocultos
endmodule

module comparador_de_termino (
  input  ver_clear,
  input  [3:0] in_2,
  input  [3:0] in_3,
  input  [3:0] in_4,
  input  [3:0] in_5,
  output id__termino
);

  wire comparator_1_eq, comparator_2_eq, comparator_3_eq, comparator_4_eq;

  Comparator #(.width(4)) comparator_1 (.a(in_2), .b(4'b0000), .eq(comparator_1_eq));  // open: gt, lt
  Comparator #(.width(4)) comparator_2 (.a(in_3), .b(4'b0000), .eq(comparator_2_eq));  // open: gt, lt
  Comparator #(.width(4)) comparator_3 (.a(in_4), .b(4'b0000), .eq(comparator_3_eq));  // open: gt, lt
  Comparator #(.width(4)) comparator_4 (.a(in_5), .b(4'b0000), .eq(comparator_4_eq));  // open: gt, lt
  and and_1 (id__termino, comparator_1_eq, comparator_2_eq, ~ver_clear, comparator_3_eq, comparator_4_eq);  // AND_Gate
endmodule

module numero_core_2 (
  input  Clock,
  input  \próximo ,
  input  [3:0] num__escolh__B,
  input  zerar_soma,
  output [3:0] \saída 
);

  D_Flip_Flop d_ff_1 (
    .clk(Clock), .D(num__escolh__B[3]), .Q(\saída [3]), .en(\próximo ), .reset(zerar_soma));  // open: Qn, preset
  D_Flip_Flop d_ff_2 (
    .clk(Clock), .D(num__escolh__B[2]), .Q(\saída [2]), .en(\próximo ), .reset(zerar_soma));  // open: Qn, preset
  D_Flip_Flop d_ff_3 (
    .clk(Clock), .D(num__escolh__B[0]), .Q(\saída [0]), .en(\próximo ), .reset(zerar_soma));  // open: Qn, preset
  D_Flip_Flop d_ff_4 (
    .clk(Clock), .D(num__escolh__B[1]), .Q(\saída [1]), .en(\próximo ), .reset(zerar_soma));  // open: Qn, preset
endmodule
