// Logisim project circuitoProjeto.circ as structural Verilog: 5 circuits, main circuit main
module main (
  input  Jogador_0,
  input  in_2,
  input  in_3,
  input  in_4,
  input  in_5,
  input  Jogador_1,
  input  in_7,
  input  in_8,
  input  in_9,
  input  Ligar_Desligar,
  output out_11,
  output out_12,
  output out_13
);

  wire convertor_para_o_displayv3_1_a, convertor_para_o_displayv3_1_b, convertor_para_o_displayv3_1_c,
       convertor_para_o_displayv3_1_d, convertor_para_o_displayv3_1_e, convertor_para_o_displayv3_1_f,
       convertor_para_o_displayv3_1_g, convertor_para_o_displayv3_2_a, convertor_para_o_displayv3_2_b,
       convertor_para_o_displayv3_2_c, convertor_para_o_displayv3_2_d, convertor_para_o_displayv3_2_e,
       convertor_para_o_displayv3_2_f, convertor_para_o_displayv3_2_g;

  _7_Segment_Display NumeroJ1 (
    .g(convertor_para_o_displayv3_1_g), .f(convertor_para_o_displayv3_1_f),
    .a(convertor_para_o_displayv3_1_a), .b(convertor_para_o_displayv3_1_b),
    .e(convertor_para_o_displayv3_1_e), .d(convertor_para_o_displayv3_1_d), .c(convertor_para_o_displayv3_1_c));  // open: dp
  _7_Segment_Display NumeroJ2 (
    .g(convertor_para_o_displayv3_2_g), .f(convertor_para_o_displayv3_2_f),
    .a(convertor_para_o_displayv3_2_a), .b(convertor_para_o_displayv3_2_b),
    .e(convertor_para_o_displayv3_2_e), .d(convertor_para_o_displayv3_2_d), .c(convertor_para_o_displayv3_2_c));  // open: dp
  Convertor_para_o_displayV3 convertor_para_o_displayv3_1 (
    .b3(Jogador_0), .b2(in_2), .b1(in_3), .b0(in_4), .a(convertor_para_o_displayv3_1_a),
    .b(convertor_para_o_displayv3_1_b), .c(convertor_para_o_displayv3_1_c),
    .d(convertor_para_o_displayv3_1_d), .e(convertor_para_o_displayv3_1_e),
    .f(convertor_para_o_displayv3_1_f), .g(convertor_para_o_displayv3_1_g));
  Convertor_para_o_displayV3 convertor_para_o_displayv3_2 (
    .b3(in_5), .b2(Jogador_1), .b1(in_7), .b0(in_8), .a(convertor_para_o_displayv3_2_a),
    .b(convertor_para_o_displayv3_2_b), .c(convertor_para_o_displayv3_2_c),
    .d(convertor_para_o_displayv3_2_d), .e(convertor_para_o_displayv3_2_e),
    .f(convertor_para_o_displayv3_2_f), .g(convertor_para_o_displayv3_2_g));
  Comb_MultiCompara comb_multicompara_1 (
    .Jogar(Ligar_Desligar), .EntradaA({Jogador_0, in_2, in_3, in_4}),
    .EntradaB({in_5, Jogador_1, in_7, in_8}), .Jogador(in_9), .\O_número_é_igual (out_11),
    .\O_número_é_maior (out_12), .\O_número_é_menor (out_13));

  // Notes on the sheet:
  //   Selecionar jogador
  //   O número é igual.
  //   O número é maior.
  //   O número é menor.
endmodule

module Multiplexador (
  input  [3:0] Entrada_A,
  input  [3:0] Entrada_B,
  input  Seletor,
  output [3:0] out_4
);

  wire [3:0] and_1_out, and_2_out;

  assign and_1_out = Entrada_A & ~{4{Seletor}};  // AND_Gate and_1, 4 bits wide
  assign and_2_out = Entrada_B & {4{Seletor}};  // AND_Gate and_2, 4 bits wide
  assign out_4 = and_1_out | and_2_out;  // OR_Gate or_1, 4 bits wide
endmodule

module Comparador_de_magnitude (
  input  [3:0] B,
  input  [3:0] A,
  output out_3,
  output out_4,
  output out_5
);

  wire and_1_out, and_2_out, and_3_out, and_4_out, and_5_out, and_6_out, and_7_out, and_8_out, and_9_out,
       and_10_out, and_11_out, and_12_out, and_13_out, and_14_out, and_15_out, and_16_out, B0_out, B1_out,
       B2_out, B3_out;

  and and_1 (and_1_out, ~A[0], ~B[0]);  // AND_Gate
  and and_2 (and_2_out, A[0], B[0]);
  and and_3 (and_3_out, ~A[1], ~B[1]);  // AND_Gate
  and and_4 (and_4_out, A[1], B[1]);
  and and_5 (and_5_out, ~A[2], ~B[2]);  // AND_Gate
  and and_6 (and_6_out, A[2], B[2]);
  and and_7 (and_7_out, ~A[3], ~B[3]);  // AND_Gate
  and and_8 (and_8_out, A[3], B[3]);
  or B0 (B0_out, and_1_out, and_2_out);
  or B1 (B1_out, and_3_out, and_4_out);
  or B2 (B2_out, and_5_out, and_6_out);
  or B3 (B3_out, and_7_out, and_8_out);
  and Igual (out_3, B0_out, B1_out, B2_out, B3_out);
  and and_9 (and_9_out, A[3], ~B[3]);  // AND_Gate
  and and_10 (and_10_out, A[2], ~B[2], B3_out);  // AND_Gate
  and and_11 (and_11_out, A[1], ~B[1], B3_out, B2_out);  // AND_Gate
  and and_12 (and_12_out, A[0], ~B[0], B2_out, B3_out, B1_out);  // AND_Gate
  and and_13 (and_13_out, ~A[3], B[3]);  // AND_Gate
  and and_14 (and_14_out, B3_out, ~A[2], B[2]);  // AND_Gate
  and and_15 (and_15_out, B3_out, B2_out, ~A[1], B[1]);  // AND_Gate
  and and_16 (and_16_out, B3_out, B2_out, B1_out, ~A[0], B[0]);  // AND_Gate
  or Maior (out_4, and_9_out, and_10_out, and_11_out, and_12_out);
  or Menor (out_5, and_13_out, and_14_out, and_15_out, and_16_out);

  // Notes on the sheet:
  //   Compara de A=B
  //   Compara se A>B
  //   Compara se A<B
endmodule

module Comb_MultiCompara (
  input  Jogar,
  input  [3:0] EntradaA,
  input  [3:0] EntradaB,
  input  Jogador,
  output \O_número_é_igual ,
  output \O_número_é_maior ,
  output \O_número_é_menor 
);

  wire Comparador_de_magnitude_out_3, Comparador_de_magnitude_out_4, Comparador_de_magnitude_out_5;
  wire [3:0] Multiplexador_out_4;

  Multiplexador Multiplexador (
    .Entrada_A(EntradaA), .Entrada_B(EntradaB), .Seletor(Jogador), .out_4(Multiplexador_out_4));
  Comparador_de_magnitude Comparador_de_magnitude (
    .B(4'b0110), .A(Multiplexador_out_4), .out_3(Comparador_de_magnitude_out_3),
    .out_4(Comparador_de_magnitude_out_4), .out_5(Comparador_de_magnitude_out_5));
  and and_1 (\O_número_é_igual , Jogar, Comparador_de_magnitude_out_3);
  and and_2 (\O_número_é_maior , Jogar, Comparador_de_magnitude_out_4);
  and and_3 (\O_número_é_menor , Jogar, Comparador_de_magnitude_out_5);
endmodule

module Convertor_para_o_displayV3 (
  input  b3,
  input  b2,
  input  b1,
  input  b0,
  output a,
  output b,
  output c,
  output d,
  output e,
  output f,
  output g
);

  wire and_1_out, and_2_out, and_3_out, and_4_out, and_5_out, and_6_out, and_7_out, and_8_out, and_9_out,
       and_10_out, and_11_out, and_12_out, and_13_out, and_14_out, and_15_out, and_16_out, and_17_out,
       and_18_out, and_19_out, and_20_out, and_21_out, and_22_out, and_23_out, and_24_out, and_25_out,
       and_26_out, and_27_out, and_28_out, and_29_out, and_30_out, and_31_out, and_32_out, and_33_out,
       or_1_out, or_2_out, or_3_out, or_4_out, or_5_out, or_6_out, or_7_out, or_8_out, or_9_out, or_10_out,
       or_11_out, or_12_out, or_13_out, or_14_out, or_15_out, or_16_out, or_17_out, or_18_out, or_19_out;

  and and_1 (and_1_out, ~b0, ~b1, ~b2, ~b3);  // AND_Gate
  and and_2 (and_2_out, ~b0, b1, ~b2, ~b3);  // AND_Gate
  and and_3 (and_3_out, b0, b1, ~b2, ~b3);  // AND_Gate
  and and_4 (and_4_out, b0, ~b1, b2, ~b3);  // AND_Gate
  and and_5 (and_5_out, ~b0, b1, b2, ~b3);  // AND_Gate
  and and_6 (and_6_out, b0, b1, b2, ~b3);  // AND_Gate
  and and_7 (and_7_out, ~b0, ~b1, ~b2, b3);  // AND_Gate
  and and_8 (and_8_out, b0, ~b1, ~b2, b3);  // AND_Gate
  and and_9 (and_9_out, ~b0, b1, ~b2, b3);  // AND_Gate
  and and_10 (and_10_out, ~b0, ~b1, b2, b3);  // AND_Gate
  and and_11 (and_11_out, ~b0, b1, b2, b3);  // AND_Gate
  and and_12 (and_12_out, b0, b1, b2, b3);
  or or_1 (or_1_out, ~b0, b1, ~b2, b3);  // OR_Gate
  or or_2 (or_2_out, b0, ~b1, ~b2, b3);  // OR_Gate
  or or_3 (or_3_out, ~b0, ~b1, b2, ~b3);  // OR_Gate
  or or_4 (or_4_out, b0, b1, ~b2, ~b3);  // OR_Gate
  or or_5 (or_5_out, b0, ~b1, ~b2, ~b3);  // OR_Gate
  or or_6 (or_6_out, ~b0, ~b1, ~b2, ~b3);  // OR_Gate
  or or_7 (or_7_out, b0, ~b1, b2, b3);  // OR_Gate
  or or_8 (or_8_out, b0, b1, ~b2, ~b3);  // OR_Gate
  or or_9 (or_9_out, b0, ~b1, ~b2, ~b3);  // OR_Gate
  or or_10 (or_10_out, ~b0, ~b1, ~b2, ~b3);  // OR_Gate
  or or_11 (or_11_out, ~b0, b1, b2, b3);  // OR_Gate
  or or_12 (or_12_out, b0, b1, ~b2, b3);  // OR_Gate
  or or_13 (or_13_out, ~b0, ~b1, ~b2, b3);  // OR_Gate
  or or_14 (or_14_out, b0, ~b1, b2, ~b3);  // OR_Gate
  or or_15 (or_15_out, ~b0, ~b1, ~b2, ~b3);  // OR_Gate
  and and_13 (and_13_out, ~b0, ~b1, ~b2, ~b3);  // AND_Gate
  and and_14 (and_14_out, ~b0, b1, ~b2, ~b3);  // AND_Gate
  and and_15 (and_15_out, ~b0, b1, b2, ~b3);  // AND_Gate
  and and_16 (and_16_out, ~b0, ~b1, ~b2, b3);  // AND_Gate
  and and_17 (and_17_out, ~b0, b1, ~b2, b3);  // AND_Gate
  and and_18 (and_18_out, b0, b1, ~b2, b3);  // AND_Gate
  and and_19 (and_19_out, ~b0, ~b1, b2, b3);  // AND_Gate
  and and_20 (and_20_out, b0, ~b1, b2, b3);  // AND_Gate
  and and_21 (and_21_out, ~b0, b1, b2, b3);  // AND_Gate
  and and_22 (and_22_out, b0, b1, b2, b3);
  and and_23 (and_23_out, ~b0, ~b1, ~b2, ~b3);  // AND_Gate
  and and_24 (and_24_out, ~b0, ~b1, b2, ~b3);  // AND_Gate
  and and_25 (and_25_out, b0, ~b1, b2, ~b3);  // AND_Gate
  and and_26 (and_26_out, ~b0, b1, b2, ~b3);  // AND_Gate
  and and_27 (and_27_out, ~b0, ~b1, ~b2, b3);  // AND_Gate
  and and_28 (and_28_out, b0, ~b1, ~b2, b3);  // AND_Gate
  and and_29 (and_29_out, ~b0, b1, ~b2, b3);  // AND_Gate
  and and_30 (and_30_out, b0, b1, ~b2, b3);  // AND_Gate
  and and_31 (and_31_out, ~b0, ~b1, b2, b3);  // AND_Gate
  and and_32 (and_32_out, ~b0, b1, b2, b3);  // AND_Gate
  and and_33 (and_33_out, b0, b1, b2, b3);
  or or_16 (or_16_out, b0, b1, b2, b3);
  or or_17 (or_17_out, ~b0, b1, b2, b3);  // OR_Gate
  or or_18 (or_18_out, ~b0, ~b1, ~b2, b3);  // OR_Gate
  or or_19 (or_19_out, b0, b1, ~b2, ~b3);  // OR_Gate
  and and_34 (b, or_1_out, or_2_out, or_3_out, or_4_out, or_5_out, or_6_out);
  and and_35 (c, or_7_out, or_8_out, or_9_out, or_10_out);
  and and_36 (d, or_11_out, or_12_out, or_13_out, or_14_out, or_15_out);
  or or_20 (e, and_13_out, and_14_out, and_15_out, and_16_out, and_17_out, and_18_out, and_19_out, and_20_out, and_21_out, and_22_out);
  and and_37 (g, or_16_out, or_17_out, or_18_out, or_19_out);
  or or_21 (f, and_23_out, and_24_out, and_25_out, and_26_out, and_27_out, and_28_out, and_29_out, and_30_out, and_31_out, and_32_out, and_33_out);
  or or_22 (a, and_1_out, and_2_out, and_3_out, and_4_out, and_5_out, and_6_out, and_7_out, and_8_out, and_9_out, and_10_out, and_11_out, and_12_out);

  // Notes on the sheet:
  //   Verificar esse
  //   Verificar esse
endmodule
